# Fritzing sketch twoWheeler (saved by Fritzing 0.9.2b)
breadboards: 1

parts:
  L298N1 = L298N DC motor driver
  Part1 = Arduino Uno (Rev3)
  U1 = LIPO-2000mAh [package=lipo-2000]
  U2 = LIPO-2000mAh [package=lipo-2000]
  DC_Mot_Enc1 = DC Motor with two-phase hall-encoder [part_number=VT-E-G25A-06-177E]
  DC_Mot_Enc2 = DC Motor with two-phase hall-encoder [part_number=VT-E-G25A-06-177E]
  Part2 = InvenSense MPU6050
  U3 = LIPO-2000mAh [package=lipo-2000]

nets:
  N1: L298N1.OUT1, DC_Mot_Enc2.pin2
  N2: L298N1.OUT2, DC_Mot_Enc2.pin1
  N3: L298N1.OUT3, DC_Mot_Enc1.pin2
  N4: L298N1.OUT4, DC_Mot_Enc1.pin1
  N5: L298N1.12V, U1.+
  N6: L298N1.GND, DC_Mot_Enc1.pin5, DC_Mot_Enc2.pin5, U3.-
  5V: L298N1.5V, Part1.5V, DC_Mot_Enc1.pin4, DC_Mot_Enc2.pin4, Part2.VCC
  N7: L298N1.ENA, Part1.D10_PWM/SS
  N8: L298N1.ENB, Part1.D5_PWM
  N9: L298N1.IN1, Part1.D9_PWM
  N10: L298N1.IN2, Part1.D8
  N11: L298N1.IN3, Part1.D7
  N12: L298N1.IN4, Part1.D6_PWM
  N13: Part1.A4/SDA, Part2.SCL
  N14: Part1.A5/SCL, Part2.SDA
  N15: Part1.D0/RX, DC_Mot_Enc1.pin3
  N16: Part1.D1/TX, DC_Mot_Enc2.pin3
  N17: Part1.D2, DC_Mot_Enc1.pin6
  N18: Part1.D3_PWM, DC_Mot_Enc2.pin6
  GND: Part1.GND, Part2.GND
  N19: U1.-, U2.+
  N20: U2.-, U3.+

notes:
  3 x 3.7 V LiPo Batteries connected in series
  Left Motor
  Right Motor
  L298N Motor Driver Board

custom parts:
  L298N DC motor driver: 2x DC motor driver with 78M05 positive voltage regulator (7..35 V) L298N: max 46 V, 2 A Set 5 V Enable jumper to enable 5 V regultor (needed for the L298N) and +5 V output at screw terminal or supply external +5 V at screw terminal Set ENA and/or ENB to +5 V to enable motor permanently or supply ENA and/or ENB with PWM signal IN1 and IN2 set rotation directory for motor A (OUT1/OUT2) IN2 and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
